# Fritzing sketch Tortoise-heat-control  (saved by Fritzing 0.9.3b)
stripboards: 1

parts:
  JP1 = Header 8 [package=1x08_smd_alt]
  JP2 = Header 8 [package=1x08_smd_alt]
  WeMos_D1_Mini1 = WeMos D1 Mini  # not connected
  Q1 = NPN-Transistor [package="TO92 [THT]"]
  R1 = Resistor [tolerance=±5% resistance=220 package=THT]
  R2 = Resistor [tolerance=±5% resistance=220 package=THT]

nets:
  N1: JP1.7, Q1.C
  N2: JP1.8, R2.Pin_0
  N3: JP2.4, R1.Pin_0
  N4: JP2.6, R2.Pin_1
  N5: Q1.B, R1.Pin_1
